# Fritzing sketch Setup (saved by Fritzing 0.9.9b)

parts:
  Bauteil1 = DPS310-KIT2GO [part_number=DPS310XTSA1]
  Bauteil2 = Bluetooth HC-05 Macho
  Bauteil3 = DPS310-KIT2GO [part_number=DPS310XTSA1]  # not connected

nets:
  GND: Bauteil1.GND, Bauteil2.GND
  +3V3: Bauteil1.+3V3, Bauteil2.VCC
  N1: Bauteil1.P2_0, Bauteil2.RXD
  N2: Bauteil1.P2_6, Bauteil2.TXD

custom parts:
  DPS310-KIT2GO: The barometric pressure sensors DPS310 offers excellent pressure noise performance and high stability with temperature.
